// Logisim project Adder.circ as structural Verilog: 11 circuits, main circuit main
module main (
  input  A,
  input  B,
  input  Cin,
  output SumAB,
  output Sum,
  output CAB,
  output Cout,
  output Ctmp
);

  xor xor_1 (SumAB, A, B);
  and and_1 (CAB, A, B);
  and and_2 (Ctmp, SumAB, Cin);
  or or_1 (Cout, CAB, Ctmp);
  xor xor_2 (Sum, SumAB, Cin);

  // Notes on the sheet:
  //   全加器
endmodule

module full_adder (
  input  A,
  input  B,
  input  Cin,
  output Sum,
  output Cout
);

  wire and_1_out, and_2_out, xor_1_out;

  xor xor_1 (xor_1_out, A, B);
  and and_1 (and_1_out, A, B);
  and and_2 (and_2_out, xor_1_out, Cin);
  or or_1 (Cout, and_1_out, and_2_out);
  xor xor_2 (Sum, xor_1_out, Cin);
endmodule

module _8bit_ripple_carry_adder (
  input  [7:0] A,
  input  [7:0] B,
  input  Cin,
  output [7:0] Result,
  output Cout
);

  wire full_adder_1_cout, full_adder_2_cout, full_adder_3_cout, full_adder_4_cout, full_adder_5_cout,
       full_adder_6_cout, full_adder_7_cout;

  full_adder full_adder_1 (.A(A[0]), .B(B[0]), .Cin(Cin), .Sum(Result[0]), .Cout(full_adder_1_cout));
  full_adder full_adder_2 (.A(A[1]), .B(B[1]), .Cin(full_adder_1_cout), .Sum(Result[1]), .Cout(full_adder_2_cout));
  full_adder full_adder_3 (.A(A[2]), .B(B[2]), .Cin(full_adder_2_cout), .Sum(Result[2]), .Cout(full_adder_3_cout));
  full_adder full_adder_4 (.A(A[3]), .B(B[3]), .Cin(full_adder_3_cout), .Sum(Result[3]), .Cout(full_adder_4_cout));
  full_adder full_adder_5 (.A(A[4]), .B(B[4]), .Cin(full_adder_4_cout), .Sum(Result[4]), .Cout(full_adder_5_cout));
  full_adder full_adder_6 (.A(A[6]), .B(B[6]), .Cin(full_adder_7_cout), .Sum(Result[6]), .Cout(full_adder_6_cout));
  full_adder full_adder_7 (.A(A[5]), .B(B[5]), .Cin(full_adder_5_cout), .Sum(Result[5]), .Cout(full_adder_7_cout));
  full_adder full_adder_8 (.A(A[7]), .B(B[7]), .Cin(full_adder_6_cout), .Sum(Result[7]), .Cout(Cout));
endmodule

module half_adder (
  input  A,
  input  B,
  output Sum,
  output Carry
);

  xor xor_1 (Sum, A, B);
  and and_1 (Carry, A, B);
endmodule

module full_adder_by_half_adder (
  input  A,
  input  B,
  input  C,
  output Carry,
  output Sum
);

  wire half_adder_1_carry, half_adder_1_sum, half_adder_2_carry;

  half_adder half_adder_1 (.A(A), .B(B), .Sum(half_adder_1_sum), .Carry(half_adder_1_carry));
  half_adder half_adder_2 (.A(half_adder_1_sum), .B(C), .Sum(Sum), .Carry(half_adder_2_carry));
  or or_1 (Carry, half_adder_1_carry, half_adder_2_carry);
endmodule

module any_of_the_bits_are_one (
  input  A0,
  input  A1,
  input  A2,
  input  A3,
  input  A4,
  input  A5,
  input  A6,
  input  A7,
  output Out
);

  wire or_1_out, or_2_out, or_3_out, or_4_out, or_5_out, or_6_out;

  or or_1 (or_1_out, A0, A1);
  or or_2 (or_2_out, A2, A3);
  or or_3 (or_3_out, A4, A5);
  or or_4 (or_4_out, A6, A7);
  or or_5 (or_5_out, or_1_out, or_2_out);
  or or_6 (or_6_out, or_3_out, or_4_out);
  or or_7 (Out, or_5_out, or_6_out);
endmodule

module all_bits_zero (
  input  A0,
  input  A1,
  input  A2,
  input  A3,
  input  A4,
  input  A5,
  input  A6,
  input  A7,
  output Out
);

  wire or_1_out, or_2_out, or_3_out, or_4_out, or_5_out, or_6_out, or_7_out;

  or or_1 (or_1_out, A0, A1);
  or or_2 (or_2_out, A2, A3);
  or or_3 (or_3_out, A4, A5);
  or or_4 (or_4_out, A6, A7);
  or or_5 (or_5_out, or_1_out, or_2_out);
  or or_6 (or_6_out, or_3_out, or_4_out);
  or or_7 (or_7_out, or_5_out, or_6_out);
  not not_1 (Out, or_7_out);
endmodule

module and_or_latch (
  input  in_1,
  input  in_2,
  input  Set,
  input  Reset,
  output Output,
  output Output_2,
  output Output_3
);

  wire not_1_out, or_2_out;

  or or_1 (Output, in_1, Output);
  and and_1 (Output_2, in_2, Output_2);
  or or_2 (or_2_out, Output_3, Set);
  not not_1 (not_1_out, Reset);
  and and_2 (Output_3, or_2_out, not_1_out);
endmodule

module gated_latch (
  input  DATA_INPUT__D,
  input  WRITE_ENABLE__E,
  output OUTPUT__Q
);

  wire and_1_out, and_2_out, not_1_out, not_2_out, or_1_out;

  not not_1 (not_1_out, DATA_INPUT__D);
  and and_1 (and_1_out, DATA_INPUT__D, WRITE_ENABLE__E);
  and and_2 (and_2_out, not_1_out, WRITE_ENABLE__E);
  or or_1 (or_1_out, OUTPUT__Q, and_1_out);
  not not_2 (not_2_out, and_2_out);
  and and_3 (OUTPUT__Q, or_1_out, not_2_out);
endmodule

module register_matrix_cell (
  input  Data_In,
  input  Row,
  input  Col,
  input  Write_Enable,
  input  Read_Enable,
  output Data_Out
);

  wire and_1_out, and_2_out, and_3_out, gated_latch_1_output__q;

  and and_1 (and_1_out, Row, Col);
  and and_2 (and_2_out, and_1_out, Write_Enable);
  and and_3 (and_3_out, and_1_out, Read_Enable);
  gated_latch gated_latch_1 (.DATA_INPUT__D(Data_In), .WRITE_ENABLE__E(and_2_out), .OUTPUT__Q(gated_latch_1_output__q));
  Multiplexer multiplexer_1 (.in1(gated_latch_1_output__q), .out(Data_Out), .sel(and_3_out));  // open: in0, en
endmodule

module register (
  input  [7:0] in_1,
  input  [7:0] in_2,
  input  Data_In,
  input  Write_Enable,
  input  Read_Enable,
  output Out
);

  register_matrix_cell register_matrix_cell_1 (
    .Data_In(Data_In), .Row(in_2[0]), .Col(in_1[0]), .Write_Enable(Write_Enable), .Read_Enable(Read_Enable),
    .Data_Out(Out));
  register_matrix_cell register_matrix_cell_2 (
    .Data_In(Data_In), .Row(in_2[1]), .Col(in_1[0]), .Write_Enable(Write_Enable), .Read_Enable(Read_Enable),
    .Data_Out(Out));
  register_matrix_cell register_matrix_cell_3 (
    .Data_In(Data_In), .Row(in_2[2]), .Col(in_1[0]), .Write_Enable(Write_Enable), .Read_Enable(Read_Enable),
    .Data_Out(Out));
  register_matrix_cell register_matrix_cell_4 (
    .Data_In(Data_In), .Row(in_2[3]), .Col(in_1[0]), .Write_Enable(Write_Enable), .Read_Enable(Read_Enable),
    .Data_Out(Out));
  register_matrix_cell register_matrix_cell_5 (
    .Data_In(Data_In), .Row(in_2[4]), .Col(in_1[0]), .Write_Enable(Write_Enable), .Read_Enable(Read_Enable),
    .Data_Out(Out));
  register_matrix_cell register_matrix_cell_6 (
    .Data_In(Data_In), .Row(in_2[5]), .Col(in_1[0]), .Write_Enable(Write_Enable), .Read_Enable(Read_Enable),
    .Data_Out(Out));
  register_matrix_cell register_matrix_cell_7 (
    .Data_In(Data_In), .Row(in_2[6]), .Col(in_1[0]), .Write_Enable(Write_Enable), .Read_Enable(Read_Enable),
    .Data_Out(Out));
  register_matrix_cell register_matrix_cell_8 (
    .Data_In(Data_In), .Row(in_2[7]), .Col(in_1[0]), .Write_Enable(Write_Enable), .Read_Enable(Read_Enable),
    .Data_Out(Out));
  register_matrix_cell register_matrix_cell_9 (
    .Data_In(Data_In), .Row(in_2[0]), .Col(in_1[1]), .Write_Enable(Write_Enable), .Read_Enable(Read_Enable),
    .Data_Out(Out));
  register_matrix_cell register_matrix_cell_10 (
    .Data_In(Data_In), .Row(in_2[1]), .Col(in_1[1]), .Write_Enable(Write_Enable), .Read_Enable(Read_Enable),
    .Data_Out(Out));
  register_matrix_cell register_matrix_cell_11 (
    .Data_In(Data_In), .Row(in_2[2]), .Col(in_1[1]), .Write_Enable(Write_Enable), .Read_Enable(Read_Enable),
    .Data_Out(Out));
  register_matrix_cell register_matrix_cell_12 (
    .Data_In(Data_In), .Row(in_2[3]), .Col(in_1[1]), .Write_Enable(Write_Enable), .Read_Enable(Read_Enable),
    .Data_Out(Out));
  register_matrix_cell register_matrix_cell_13 (
    .Data_In(Data_In), .Row(in_2[4]), .Col(in_1[1]), .Write_Enable(Write_Enable), .Read_Enable(Read_Enable),
    .Data_Out(Out));
  register_matrix_cell register_matrix_cell_14 (
    .Data_In(Data_In), .Row(in_2[5]), .Col(in_1[1]), .Write_Enable(Write_Enable), .Read_Enable(Read_Enable),
    .Data_Out(Out));
  register_matrix_cell register_matrix_cell_15 (
    .Data_In(Data_In), .Row(in_2[6]), .Col(in_1[1]), .Write_Enable(Write_Enable), .Read_Enable(Read_Enable),
    .Data_Out(Out));
  register_matrix_cell register_matrix_cell_16 (
    .Data_In(Data_In), .Row(in_2[7]), .Col(in_1[1]), .Write_Enable(Write_Enable), .Read_Enable(Read_Enable),
    .Data_Out(Out));
  register_matrix_cell register_matrix_cell_17 (
    .Data_In(Data_In), .Row(in_2[0]), .Col(in_1[2]), .Write_Enable(Write_Enable), .Read_Enable(Read_Enable),
    .Data_Out(Out));
  register_matrix_cell register_matrix_cell_18 (
    .Data_In(Data_In), .Row(in_2[1]), .Col(in_1[2]), .Write_Enable(Write_Enable), .Read_Enable(Read_Enable),
    .Data_Out(Out));
  register_matrix_cell register_matrix_cell_19 (
    .Data_In(Data_In), .Row(in_2[2]), .Col(in_1[2]), .Write_Enable(Write_Enable), .Read_Enable(Read_Enable),
    .Data_Out(Out));
  register_matrix_cell register_matrix_cell_20 (
    .Data_In(Data_In), .Row(in_2[3]), .Col(in_1[2]), .Write_Enable(Write_Enable), .Read_Enable(Read_Enable),
    .Data_Out(Out));
  register_matrix_cell register_matrix_cell_21 (
    .Data_In(Data_In), .Row(in_2[4]), .Col(in_1[2]), .Write_Enable(Write_Enable), .Read_Enable(Read_Enable),
    .Data_Out(Out));
  register_matrix_cell register_matrix_cell_22 (
    .Data_In(Data_In), .Row(in_2[5]), .Col(in_1[2]), .Write_Enable(Write_Enable), .Read_Enable(Read_Enable),
    .Data_Out(Out));
  register_matrix_cell register_matrix_cell_23 (
    .Data_In(Data_In), .Row(in_2[6]), .Col(in_1[2]), .Write_Enable(Write_Enable), .Read_Enable(Read_Enable),
    .Data_Out(Out));
  register_matrix_cell register_matrix_cell_24 (
    .Data_In(Data_In), .Row(in_2[7]), .Col(in_1[2]), .Write_Enable(Write_Enable), .Read_Enable(Read_Enable),
    .Data_Out(Out));
  register_matrix_cell register_matrix_cell_25 (
    .Data_In(Data_In), .Row(in_2[0]), .Col(in_1[3]), .Write_Enable(Write_Enable), .Read_Enable(Read_Enable),
    .Data_Out(Out));
  register_matrix_cell register_matrix_cell_26 (
    .Data_In(Data_In), .Row(in_2[1]), .Col(in_1[3]), .Write_Enable(Write_Enable), .Read_Enable(Read_Enable),
    .Data_Out(Out));
  register_matrix_cell register_matrix_cell_27 (
    .Data_In(Data_In), .Row(in_2[2]), .Col(in_1[3]), .Write_Enable(Write_Enable), .Read_Enable(Read_Enable),
    .Data_Out(Out));
  register_matrix_cell register_matrix_cell_28 (
    .Data_In(Data_In), .Row(in_2[3]), .Col(in_1[3]), .Write_Enable(Write_Enable), .Read_Enable(Read_Enable),
    .Data_Out(Out));
  register_matrix_cell register_matrix_cell_29 (
    .Data_In(Data_In), .Row(in_2[4]), .Col(in_1[3]), .Write_Enable(Write_Enable), .Read_Enable(Read_Enable),
    .Data_Out(Out));
  register_matrix_cell register_matrix_cell_30 (
    .Data_In(Data_In), .Row(in_2[5]), .Col(in_1[3]), .Write_Enable(Write_Enable), .Read_Enable(Read_Enable),
    .Data_Out(Out));
  register_matrix_cell register_matrix_cell_31 (
    .Data_In(Data_In), .Row(in_2[6]), .Col(in_1[3]), .Write_Enable(Write_Enable), .Read_Enable(Read_Enable),
    .Data_Out(Out));
  register_matrix_cell register_matrix_cell_32 (
    .Data_In(Data_In), .Row(in_2[7]), .Col(in_1[3]), .Write_Enable(Write_Enable), .Read_Enable(Read_Enable),
    .Data_Out(Out));
  register_matrix_cell register_matrix_cell_33 (
    .Data_In(Data_In), .Row(in_2[0]), .Col(in_1[4]), .Write_Enable(Write_Enable), .Read_Enable(Read_Enable),
    .Data_Out(Out));
  register_matrix_cell register_matrix_cell_34 (
    .Data_In(Data_In), .Row(in_2[1]), .Col(in_1[4]), .Write_Enable(Write_Enable), .Read_Enable(Read_Enable),
    .Data_Out(Out));
  register_matrix_cell register_matrix_cell_35 (
    .Data_In(Data_In), .Row(in_2[2]), .Col(in_1[4]), .Write_Enable(Write_Enable), .Read_Enable(Read_Enable),
    .Data_Out(Out));
  register_matrix_cell register_matrix_cell_36 (
    .Data_In(Data_In), .Row(in_2[3]), .Col(in_1[4]), .Write_Enable(Write_Enable), .Read_Enable(Read_Enable),
    .Data_Out(Out));
  register_matrix_cell register_matrix_cell_37 (
    .Data_In(Data_In), .Row(in_2[4]), .Col(in_1[4]), .Write_Enable(Write_Enable), .Read_Enable(Read_Enable),
    .Data_Out(Out));
  register_matrix_cell register_matrix_cell_38 (
    .Data_In(Data_In), .Row(in_2[5]), .Col(in_1[4]), .Write_Enable(Write_Enable), .Read_Enable(Read_Enable),
    .Data_Out(Out));
  register_matrix_cell register_matrix_cell_39 (
    .Data_In(Data_In), .Row(in_2[6]), .Col(in_1[4]), .Write_Enable(Write_Enable), .Read_Enable(Read_Enable),
    .Data_Out(Out));
  register_matrix_cell register_matrix_cell_40 (
    .Data_In(Data_In), .Row(in_2[7]), .Col(in_1[4]), .Write_Enable(Write_Enable), .Read_Enable(Read_Enable),
    .Data_Out(Out));
  register_matrix_cell register_matrix_cell_41 (
    .Data_In(Data_In), .Row(in_2[0]), .Col(in_1[5]), .Write_Enable(Write_Enable), .Read_Enable(Read_Enable),
    .Data_Out(Out));
  register_matrix_cell register_matrix_cell_42 (
    .Data_In(Data_In), .Row(in_2[1]), .Col(in_1[5]), .Write_Enable(Write_Enable), .Read_Enable(Read_Enable),
    .Data_Out(Out));
  register_matrix_cell register_matrix_cell_43 (
    .Data_In(Data_In), .Row(in_2[2]), .Col(in_1[5]), .Write_Enable(Write_Enable), .Read_Enable(Read_Enable),
    .Data_Out(Out));
  register_matrix_cell register_matrix_cell_44 (
    .Data_In(Data_In), .Row(in_2[3]), .Col(in_1[5]), .Write_Enable(Write_Enable), .Read_Enable(Read_Enable),
    .Data_Out(Out));
  register_matrix_cell register_matrix_cell_45 (
    .Data_In(Data_In), .Row(in_2[4]), .Col(in_1[5]), .Write_Enable(Write_Enable), .Read_Enable(Read_Enable),
    .Data_Out(Out));
  register_matrix_cell register_matrix_cell_46 (
    .Data_In(Data_In), .Row(in_2[5]), .Col(in_1[5]), .Write_Enable(Write_Enable), .Read_Enable(Read_Enable),
    .Data_Out(Out));
  register_matrix_cell register_matrix_cell_47 (
    .Data_In(Data_In), .Row(in_2[6]), .Col(in_1[5]), .Write_Enable(Write_Enable), .Read_Enable(Read_Enable),
    .Data_Out(Out));
  register_matrix_cell register_matrix_cell_48 (
    .Data_In(Data_In), .Row(in_2[7]), .Col(in_1[5]), .Write_Enable(Write_Enable), .Read_Enable(Read_Enable),
    .Data_Out(Out));
  register_matrix_cell register_matrix_cell_49 (
    .Data_In(Data_In), .Row(in_2[0]), .Col(in_1[6]), .Write_Enable(Write_Enable), .Read_Enable(Read_Enable),
    .Data_Out(Out));
  register_matrix_cell register_matrix_cell_50 (
    .Data_In(Data_In), .Row(in_2[1]), .Col(in_1[6]), .Write_Enable(Write_Enable), .Read_Enable(Read_Enable),
    .Data_Out(Out));
  register_matrix_cell register_matrix_cell_51 (
    .Data_In(Data_In), .Row(in_2[2]), .Col(in_1[6]), .Write_Enable(Write_Enable), .Read_Enable(Read_Enable),
    .Data_Out(Out));
  register_matrix_cell register_matrix_cell_52 (
    .Data_In(Data_In), .Row(in_2[3]), .Col(in_1[6]), .Write_Enable(Write_Enable), .Read_Enable(Read_Enable),
    .Data_Out(Out));
  register_matrix_cell register_matrix_cell_53 (
    .Data_In(Data_In), .Row(in_2[4]), .Col(in_1[6]), .Write_Enable(Write_Enable), .Read_Enable(Read_Enable),
    .Data_Out(Out));
  register_matrix_cell register_matrix_cell_54 (
    .Data_In(Data_In), .Row(in_2[5]), .Col(in_1[6]), .Write_Enable(Write_Enable), .Read_Enable(Read_Enable),
    .Data_Out(Out));
  register_matrix_cell register_matrix_cell_55 (
    .Data_In(Data_In), .Row(in_2[6]), .Col(in_1[6]), .Write_Enable(Write_Enable), .Read_Enable(Read_Enable),
    .Data_Out(Out));
  register_matrix_cell register_matrix_cell_56 (
    .Data_In(Data_In), .Row(in_2[7]), .Col(in_1[6]), .Write_Enable(Write_Enable), .Read_Enable(Read_Enable),
    .Data_Out(Out));
  register_matrix_cell register_matrix_cell_57 (
    .Data_In(Data_In), .Row(in_2[0]), .Col(in_1[7]), .Write_Enable(Write_Enable), .Read_Enable(Read_Enable),
    .Data_Out(Out));
  register_matrix_cell register_matrix_cell_58 (
    .Data_In(Data_In), .Row(in_2[1]), .Col(in_1[7]), .Write_Enable(Write_Enable), .Read_Enable(Read_Enable),
    .Data_Out(Out));
  register_matrix_cell register_matrix_cell_59 (
    .Data_In(Data_In), .Row(in_2[2]), .Col(in_1[7]), .Write_Enable(Write_Enable), .Read_Enable(Read_Enable),
    .Data_Out(Out));
  register_matrix_cell register_matrix_cell_60 (
    .Data_In(Data_In), .Row(in_2[3]), .Col(in_1[7]), .Write_Enable(Write_Enable), .Read_Enable(Read_Enable),
    .Data_Out(Out));
  register_matrix_cell register_matrix_cell_61 (
    .Data_In(Data_In), .Row(in_2[4]), .Col(in_1[7]), .Write_Enable(Write_Enable), .Read_Enable(Read_Enable),
    .Data_Out(Out));
  register_matrix_cell register_matrix_cell_62 (
    .Data_In(Data_In), .Row(in_2[5]), .Col(in_1[7]), .Write_Enable(Write_Enable), .Read_Enable(Read_Enable),
    .Data_Out(Out));
  register_matrix_cell register_matrix_cell_63 (
    .Data_In(Data_In), .Row(in_2[6]), .Col(in_1[7]), .Write_Enable(Write_Enable), .Read_Enable(Read_Enable),
    .Data_Out(Out));
  register_matrix_cell register_matrix_cell_64 (
    .Data_In(Data_In), .Row(in_2[7]), .Col(in_1[7]), .Write_Enable(Write_Enable), .Read_Enable(Read_Enable),
    .Data_Out(Out));
endmodule
